// Logisim project micro.circ as structural Verilog: 1 circuit, main circuit EV20_Superescalar
module EV20_Superescalar (
);

  wire button_1_out, CLK, CLK2, CLK3, CLK4, dipswitch_1_sw1, not_1_out, not_2_out, not_3_out, undriven,
       undriven_2, undriven_3;

  DipSwitch #(.number(2)) dipswitch_1 (.sw1(dipswitch_1_sw1));  // open: sw2
  Button button_1 (.out(button_1_out));
  ClockGenerator clocks (
    .Auto(dipswitch_1_sw1), .ManualCLK(button_1_out), .CLK(CLK), .CLK2(CLK2), .CLK3(CLK3), .CLK4(CLK4));
  Register #(.width(16)) BusB_ALU (.D(16'hcccc));  // open: en, clk, Q, clr
  not not_1 (not_1_out, undriven);
  Pipeline_register ALU (
    .S_low_P_high(1'b0), .Hold(not_1_out));  // open: ALUC_IN, SH_IN, Kmx_IN, CLK, MRyMB_IN, B_bus_IN, T_bus_IN, C_bus_IN, Serial_IN, A_bus_IN, D_Address_IN, ALUC_OUT, SH_OUT, Kmx_OUT, MRyMB_OUT, B_bus_OUT, T_bus_OUT, C_bus_OUT, Serial_OUT, A_bus_OUT, D_Address_OUT
  Register #(.width(16)) BusA_ALU (.D(16'hbbbb));  // open: en, clk, Q, clr
  not not_2 (not_2_out, undriven_2);
  // Micro_Instruction_ROM micro_instruction_rom_1: pin names not known
  Pipeline_register pipeline_register_1 (
    .S_low_P_high(1'b0), .Hold(not_2_out));  // open: ALUC_IN, SH_IN, Kmx_IN, CLK, MRyMB_IN, B_bus_IN, T_bus_IN, C_bus_IN, Serial_IN, A_bus_IN, D_Address_IN, ALUC_OUT, SH_OUT, Kmx_OUT, MRyMB_OUT, B_bus_OUT, T_bus_OUT, C_bus_OUT, Serial_OUT, A_bus_OUT, D_Address_OUT
  Pipeline_register pipeline_register_2 (
    .S_low_P_high(1'b0), .Serial_IN(32'h10001), .D_Address_IN(10'h2aa));  // open: ALUC_IN, SH_IN, Kmx_IN, CLK, MRyMB_IN, B_bus_IN, T_bus_IN, C_bus_IN, A_bus_IN, Hold, ALUC_OUT, SH_OUT, Kmx_OUT, MRyMB_OUT, B_bus_OUT, T_bus_OUT, C_bus_OUT, Serial_OUT, A_bus_OUT, D_Address_OUT
  // UC1 uc1_1: pin names not known
  not not_3 (not_3_out, undriven_3);
  Register #(.width(16)) BusA_LS (.D(16'haaaa));  // open: en, clk, Q, clr
  Pipeline_register LoadStore (
    .S_low_P_high(1'b0), .Hold(not_3_out));  // open: ALUC_IN, SH_IN, Kmx_IN, CLK, MRyMB_IN, B_bus_IN, T_bus_IN, C_bus_IN, Serial_IN, A_bus_IN, D_Address_IN, ALUC_OUT, SH_OUT, Kmx_OUT, MRyMB_OUT, B_bus_OUT, T_bus_OUT, C_bus_OUT, Serial_OUT, A_bus_OUT, D_Address_OUT
endmodule
